# Fritzing sketch pcb (saved by Fritzing 0.9.3b)
circuit board: 4.02467cm x 2.88599cm
breadboards: 1

parts:
  R6 = Resistor [tolerance=±5% resistance=10k package=THT]
  R1 = Resistor [tolerance=±5% resistance=56k package=THT]
  U1 = TRANSISTOR_NPN [package=to-92]
  U2 = TRANSISTOR_NPN_2 [package=to-92]
  R2 = Resistor [tolerance=±5% resistance=56k package=THT]
  R4 = Resistor [tolerance=±5% resistance=10k package=THT]
  R7 = Resistor [tolerance=±5% resistance=10k package=THT]
  R5 = Resistor [tolerance=±5% resistance=10k package=THT]
  U3 = mystery part, 3 pins [chip_label=ALIMENTAZIONE]
  U6 = mystery part, 3 pins [chip_label=ANALOG]
  U7 = mystery part, 3 pins [chip_label=LM35]
  U8 = mystery part, 2 pins [chip_label=GSR]
  U4 = mystery part, 2 pins [chip_label=DIGITAL]
  R3 = Resistor [tolerance=±5% resistance=10k package=THT]
  D1 = Rectifier Diode [part_number=1N4001 package="300 mil [THT]"]

nets:
  N1: R6.Pin_0, R7.Pin_1, U6.pin2, U8.pin2
  N2: R6.Pin_1, R5.Pin_0
  N3: R1.Pin_0, R2.Pin_0
  N4: R1.Pin_1, R7.Pin_0, U3.pin2, U7.pin2
  N5: U1.E, U3.pin3
  N6: U1.B, R4.Pin_1
  N7: U1.C, U7.pin1
  N8: U2.C, D1.anode
  N9: U2.B, R3.Pin_0
  N10: U2.E, U3.pin1
  N11: R2.Pin_1, U6.pin3, U8.pin1
  N12: R4.Pin_0, U4.pin1
  N13: R5.Pin_1, D1.cathode
  N14: U6.pin1, U7.pin3
  N15: U4.pin2, R3.Pin_1
